# Fritzing sketch HW_4_Gozde_Asli_ (saved by Fritzing 1.0.3b)
breadboards: 1

parts:
  R1 = Resistor [tolerance=±5% power=0.25W resistance=330 package=THT]
  R2 = Resistor [tolerance=±5% power=0.25W resistance=330 package=THT]
  R3 = Resistor [tolerance=±5% power=0.25W resistance=330 package=THT]
  J1 = STM32 Nucleo boards
  R4 = Resistor [tolerance=±5% power=0.25W resistance=10k package=THT]
  Q1 = NPN-Transistor [package="TO92 [THT]"]
  R5 = Photocell (LDR) [power=0.25W dark_resistance_@0.01lx=300kΩ light_resistance_@100lx=400Ω luminance=10lx package=THT]
  LED1 = RGB LED - (4 legs) [color="Red (633nm)" current=0.030A package="5 mm [THT]"]
  SG1 = Buzzer 12mm [part_number=COM-07950 package=buzzer-12mm-ns]
  R6 = Rotary Potentiometer (Large) [maximum_resistance=1kΩ knob_status=50% power=0.5W package=THT]

nets:
  N1: R1.Pin_0, J1.D6_PWM
  N2: R1.Pin_1, LED1.red_cathode
  N3: R2.Pin_0, J1.D5_PWM
  N4: R2.Pin_1, LED1.green_cathode
  N5: R3.Pin_0, J1.D3_PWM
  N6: R3.Pin_1, LED1.blue_cathode
  N7: J1.A0, R4.Pin_0, R5.pin_1
  N8: J1.PA11, R6.wiper
  N9: J1.3V3, R4.Pin_1
  N10: J1.5V, LED1.common_anode, SG1.1
  N11: J1.GND, Q1.E, R5.pin_0, R6.leg2
  N12: Q1.B, R6.leg1
  N13: Q1.C, SG1.2

custom parts:
  Buzzer 12mm: Buzzer 12mm Spark Fun Electronics SKU : Comp-Buzzer Through hole This is a small 12mm round speaker that operates around the audible 2kHz range. You can use these speakers to create simple music or user interfaces. This is not a true piezoelectric speaker but behaves similarly. Instead of a piezoelectric crystal that vibrates with an electric current, this tiny speaker uses an electromagnet to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
